# Fritzing sketch schematic (saved by Fritzing 0.9.3b)
breadboards: 1

parts:
  U1 = ESP8266 NodeMCU LoLin module
  Componente1 = Solar Cell
  Componente2 = Solar Cell
  TP1 = TP4056 [chip_label=TP4056 package="DIP (Dual Inline) [THT]"]
  VCC1 = 4 x AAA Battery Mount
  Reg1 = DC-DC CONVERTER [part_number=80633 package=dc-dc_converter]
  PART1 = SparkFun Soil Moisture Sensor [part_number=SEN-13322]

nets:
  GND: U1.GND, Reg1.OUT-, PART1.GND
  VIN: U1.Vin, Reg1.OUT+, PART1.VCC
  N1: U1.A0, PART1.SIG
  N2: Componente1.+, Componente2.+, TP1.pin1
  N3: Componente1.-, Componente2.-, TP1.pin2
  N4: TP1.pin3, Reg1.IN+
  N5: TP1.pin4, VCC1.+
  N6: TP1.pin5, VCC1.-
  N7: TP1.pin6, Reg1.IN-

custom parts:
  ESP8266 NodeMCU LoLin module: ESP8266 based NodeMCU
  TP4056: A DIP stand-in part for whatever IC you want. With 6 pins on a 300mil dual inline package (DIP) footprint.
  DC-DC CONVERTER: WYHP 5A constant current/voltage manufactured by Shenzhen Weiyapuhua Technology Co., Ltd
  SparkFun Soil Moisture Sensor: The SparkFun Soil Moisture Sensor is a simple breakout for measuring the moisture in soil and similar materials.
